# Fritzing sketch arduino-esp8266-serialComm (saved by Fritzing 0.9.3b)
breadboards: 1

parts:
  Part1 = Arduino Nano (Rev3.0)
  U1 = NodeMCU V1.0

nets:
  N1: Part1.D1/TX, U1.RX
  N2: Part1.D0/RX, U1.TX
  GND: Part1.GND, U1.GND

notes:
  ESP8266-Arduino Serial interface

custom parts:
  NodeMCU V1.0: ESP8266 based NodeMCU
